// Logisim project cpu.circ as structural Verilog: 1 circuit, main circuit cpu
module cpu (
  input  clk,
  input  [31:0] Instruction,
  input  [31:0] MemReadData,
  output [31:0] MemAddress,
  output [31:0] ProgramCounter,
  output [31:0] ra,
  output [31:0] sp,
  output [31:0] t0,
  output [31:0] t1,
  output [31:0] t2,
  output [31:0] s0,
  output [31:0] s1,
  output [31:0] a0,
  output [3:0] MemWriteMask,
  output [31:0] MemWriteData
);

  wire ASel, BrEq, BrLt, BrUn, BSel, MemEn, PCSel, RegWEn;
  wire [1:0] WBSel;
  wire [2:0] ImmSel;
  wire [3:0] ALUSel;
  wire [31:0] A_Value, adder_1_out, B_Value, DataToReg, EXINS, EXPC_q, EXRD1, EXRD2, IDINS, IDPC_q,
       immedimate, MAALU, MAINS, MAPC, MARD2, PCPlus4, PCValue, ReadData1, ReadData2, WBDATA, WBData_t, WBINS;

  Register #(.width(32)) PC (.D(PCValue), .clk(clk), .Q(ProgramCounter));  // open: en, clr
  Adder #(.width(32)) adder_1 (.a(ProgramCounter), .b(32'h4), .out(adder_1_out));  // open: cin, cout
  Multiplexer #(.width(32)) multiplexer_1 (.in0(adder_1_out), .in1(MemAddress), .out(PCValue), .sel(PCSel));
  control_logic control_logic_1 (
    .Instruction(IDINS), .BrEq(BrEq), .BrLt(BrLt), .PCSel(PCSel), .RegWEn(RegWEn), .ImmSel(ImmSel),
    .BrUn(BrUn), .ASel(ASel), .BSel(BSel), .ALUSel(ALUSel), .MemWEn(MemEn), .WBSel(WBSel));
  imm_gen imm_gen_1 (.Instruction(EXINS), .ImmSel(ImmSel), .Immediate(immedimate));
  regfile regfile_1 (
    .ReadIndex1(IDINS[19:15]), .ReadIndex2(IDINS[24:20]), .WriteIndex(IDINS[11:7]), .WriteData(WBDATA),
    .RegWEn(RegWEn), .clk(clk), .ra(ra), .sp(sp), .t0(t0), .t1(t1), .t2(t2), .s0(s0), .s1(s1), .a0(a0),
    .ReadData1(ReadData1), .ReadData2(ReadData2));
  Register #(.width(32)) register_1 (.D(MemAddress), .clk(clk), .Q(MAALU));  // open: en, clr
  Register #(.width(32)) register_2 (.D(WBData_t), .clk(clk), .Q(WBDATA));  // open: en, clr
  Register #(.width(32)) u_IDINS (.D(Instruction), .clk(clk), .Q(IDINS));  // open: en, clr
  Register #(.width(32)) IDPC (.D(ProgramCounter), .clk(clk), .Q(IDPC_q));  // open: en, clr
  Register #(.width(32)) register_3 (.D(ReadData1), .clk(clk), .Q(EXRD1));  // open: en, clr
  Register #(.width(32)) register_4 (.D(ReadData2), .clk(clk), .Q(EXRD2));  // open: en, clr
  Register #(.width(32)) EXPC (.D(IDPC_q), .clk(clk), .Q(EXPC_q));  // open: en, clr
  Register #(.width(32)) register_5 (.D(EXRD2), .clk(clk), .Q(MARD2));  // open: en, clr
  alu alu_1 (.A(A_Value), .B(B_Value), .ALUSel(ALUSel), .ALUResult(MemAddress));
  branch_comp branch_comp_1 (.BrData1(ReadData1), .BrData2(ReadData2), .BrUn(BrUn), .BrEq(BrEq), .BrLt(BrLt));
  Register #(.width(32)) u_EXINS (.D(IDINS), .clk(clk), .Q(EXINS));  // open: en, clr
  Register #(.width(32)) u_MAINS (.D(EXINS), .clk(clk), .Q(MAINS));  // open: en, clr
  Register #(.width(32)) u_MAPC (.D(EXPC_q), .clk(clk), .Q(MAPC));  // open: en, clr
  Register #(.width(32)) u_WBINS (.D(MAINS), .clk(clk), .Q(WBINS));  // open: en, clr
  Multiplexer #(.width(32)) multiplexer_2 (.in0(EXRD2), .in1(immedimate), .out(B_Value), .sel(BSel));
  Multiplexer #(.width(32)) multiplexer_3 (.in0(EXRD1), .in1(ProgramCounter), .out(A_Value), .sel(ASel));
  partial_store partial_store_1 (
    .Instruction(MAINS), .MemAddress(MemAddress), .DataFromReg(MARD2), .MemWEn(MemEn),
    .MemWriteMask(MemWriteMask), .DataToMem(MemWriteData));
  partial_load partial_load_1 (
    .Instruction(MAINS), .MemAddress(MAALU), .DataFromMem(MemReadData), .DataToReg(DataToReg));
  Multiplexer #(.select(2), .width(32)) multiplexer_4 (
    .in0(DataToReg), .in1(MAALU), .in2(PCPlus4), .out(WBData_t), .sel(WBSel));  // open: in3
  Adder #(.width(32)) adder_2 (.a(MAPC), .b(32'h4), .out(PCPlus4));  // open: cin, cout

  // Other names for the same wires on the sheet: ALUResult[31:0] = MemAddress; rd[4:0] = IDINS[11:7];
  //   rs1[4:0] = IDINS[19:15]; rs2[4:0] = IDINS[24:20]

  // Notes on the sheet:
  //   To IMEM
  //   IMEM (do **NOT** move this)
  //   From IMEM
  //   Inputs/Outputs for testing. Do **NOT** move these.
  //   It is OK to move the PC, RegFile, ALU, MEM, Branch Comp, Imm Gen, Partial Load, Partial Store and Control Logic to wherever is most convenient for you when constructing your CPU, and to delete this text
  //   To DMEM
  //   DMEM (do **NOT** move this)
  //   From DMEM
endmodule
